// Digital circuit 1 new half add.dig as structural Verilog
module _1_new_half_add (
  input  A,
  input  b,
  input  in_3,
  output out,
  output cout
);

  wire xor_2_out;

  xor xor_1 (out, A, b);
  xor xor_2 (xor_2_out, in_3, A);
  and and_1 (cout, xor_2_out, b);
endmodule
