// Digital circuit 16 add 1.dig as structural Verilog
module _16_add_1 (
  input  cin,
  input  _1,
  input  _2,
  input  _3,
  input  _4,
  input  _5,
  input  _6,
  input  _7,
  input  _8,
  input  _9,
  input  _10,
  input  _11,
  input  _12,
  input  _13,
  input  _14,
  input  _15,
  input  _16,
  output out1,
  output out2,
  output out3,
  output out4,
  output out5,
  output out6,
  output out7,
  output out8,
  output out9,
  output out10,
  output out11,
  output out12,
  output out13,
  output out14,
  output out15,
  output out16
);

  wire and_1_out, and_2_out, and_3_out, and_4_out, and_5_out, and_6_out, and_7_out, and_8_out, and_9_out,
       and_10_out, and_11_out, and_12_out, and_13_out, and_14_out, and_15_out;

  xor xor_1 (out1, _1, cin);
  and and_1 (and_1_out, _1, cin);
  xor xor_2 (out2, _2, and_1_out);
  and and_2 (and_2_out, _2, and_1_out);
  xor xor_3 (out3, _3, and_2_out);
  and and_3 (and_3_out, _3, and_2_out);
  xor xor_4 (out4, _4, and_3_out);
  and and_4 (and_4_out, _4, and_3_out);
  xor xor_5 (out5, _5, and_4_out);
  and and_5 (and_5_out, _5, and_4_out);
  xor xor_6 (out6, _6, and_5_out);
  and and_6 (and_6_out, _6, and_5_out);
  xor xor_7 (out7, _7, and_6_out);
  and and_7 (and_7_out, _7, and_6_out);
  xor xor_8 (out8, _8, and_7_out);
  and and_8 (and_8_out, _8, and_7_out);
  xor xor_9 (out9, _9, and_8_out);
  and and_9 (and_9_out, _9, and_8_out);
  xor xor_10 (out10, _10, and_9_out);
  and and_10 (and_10_out, _10, and_9_out);
  xor xor_11 (out11, _11, and_10_out);
  and and_11 (and_11_out, _11, and_10_out);
  xor xor_12 (out12, _12, and_11_out);
  and and_12 (and_12_out, _12, and_11_out);
  xor xor_13 (out13, _13, and_12_out);
  and and_13 (and_13_out, _13, and_12_out);
  xor xor_14 (out14, _14, and_13_out);
  and and_14 (and_14_out, _14, and_13_out);
  xor xor_15 (out15, _15, and_14_out);
  and and_15 (and_15_out, _15, and_14_out);
  xor xor_16 (out16, _16, and_15_out);
endmodule
