// Digital circuit 16bit adder.dig as structural Verilog
module _16bit_adder (
  input  A1,
  input  A2,
  input  A3,
  input  A4,
  input  in_22,
  input  B0,
  input  B1,
  input  B2,
  input  B3,
  input  B4,
  input  B5,
  input  B6,
  input  B7,
  input  A5,
  input  A6,
  input  A7,
  input  A8,
  input  B8,
  input  B9,
  input  B10,
  input  B11,
  input  B12,
  input  B13,
  input  B14,
  input  B15,
  input  A9,
  input  A10,
  input  A11,
  input  A12,
  input  A13,
  input  A14,
  input  A15,
  input  A16,
  input  cin,
  output p1,
  output p2,
  output p3,
  output p4,
  output p5,
  output p6,
  output p7,
  output p8,
  output cout,
  output p9,
  output p10,
  output p11,
  output p12,
  output p13,
  output p14,
  output p15,
  output p16
);

  wire _8bit_adder_2_p9;

  // _8bit_adder _8bit_adder_1: pin names not known; wires that end beside it: A16, A15, A14, A13, A12, A11, A10, A9, cout, in_22, B15, B14, B13, B12, B11, B10, B9, B8
  // _8bit_adder _8bit_adder_2: pin names not known; wires that end beside it: A8, A7, A6, A5, A4, A3, A2, A1, _8bit_adder_2_p9, in_22, B7, B6, B5, B4, B3, B2, B1, B0
endmodule
