// Digital circuit 4 bit multiplier.dig as structural Verilog
module _4_bit_multiplier (
  input  A0,
  input  A1,
  input  A2,
  input  A3,
  input  B0,
  input  B1,
  input  B2,
  input  B3,
  output p0,
  output p1,
  output p2,
  output p3,
  output p4,
  output p5,
  output p6,
  output p7
);

  wire _4bit_adder_1_p11, _4bit_adder_2_p7, _4bit_adder_2_p8, _4bit_adder_2_p9, _4bit_adder_2_p11,
       _4bit_adder_3_p7, _4bit_adder_3_p8, _4bit_adder_3_p9, and_1_out, and_2_out, and_3_out, and_4_out,
       and_5_out, and_6_out, and_7_out, and_9_out, and_10_out, and_11_out, and_12_out, and_13_out,
       and_14_out, and_15_out, and_16_out;

  and and_1 (and_1_out, B1, A0);
  and and_2 (and_2_out, B1, A1);
  and and_3 (and_3_out, B1, A2);
  and and_4 (and_4_out, B1, A3);
  and and_5 (and_5_out, A3, B0);
  and and_6 (and_6_out, A2, B0);
  and and_7 (and_7_out, A1, B0);
  and and_8 (p0, A0, B0);
  // _4bit_adder _4bit_adder_1: pin names not known; wires that end beside it: and_1_out, and_2_out, and_3_out, and_4_out, 1'b0, and_7_out, and_6_out, and_5_out, 1'b0, 1'b0, _4bit_adder_1_p11, p1
  and and_9 (and_9_out, B2, A0);
  and and_10 (and_10_out, A1, B2);
  and and_11 (and_11_out, A2, B2);
  and and_12 (and_12_out, A3, B2);
  // _4bit_adder _4bit_adder_2: pin names not known; wires that end beside it: and_9_out, and_10_out, and_11_out, and_12_out, 1'b0, _4bit_adder_1_p11, _4bit_adder_2_p7, _4bit_adder_2_p8, _4bit_adder_2_p9, 1'b0, _4bit_adder_2_p11, p2
  and and_13 (and_13_out, A0, B3);
  and and_14 (and_14_out, A1, B3);
  and and_15 (and_15_out, A2, B3);
  and and_16 (and_16_out, A3, B3);
  // _4bit_adder _4bit_adder_3: pin names not known; wires that end beside it: and_13_out, and_14_out, and_15_out, and_16_out, 1'b0, _4bit_adder_2_p11, _4bit_adder_3_p7, _4bit_adder_3_p8, _4bit_adder_3_p9, 1'b0, p4, p3
endmodule
