// Digital circuit 4bit adder.dig as structural Verilog
module _4bit_adder (
  input  A0,
  input  A1,
  input  A2,
  input  A3,
  input  in_5,
  input  cin,
  input  B0,
  input  B1,
  input  B2,
  input  B3,
  output p1,
  output p2,
  output p3,
  output p4,
  output cout
);

  wire full_aadder_and_sub_1_bit_1_p6, full_aadder_and_sub_1_bit_2_p6, full_aadder_and_sub_1_bit_3_p6;

  // full_aadder_and_sub_1_bit full_aadder_and_sub_1_bit_1: pin names not known; wires that end beside it: A0, B0, cin, in_5, p1, full_aadder_and_sub_1_bit_1_p6
  // full_aadder_and_sub_1_bit full_aadder_and_sub_1_bit_2: pin names not known; wires that end beside it: A1, B1, full_aadder_and_sub_1_bit_1_p6, in_5, p2, full_aadder_and_sub_1_bit_2_p6
  // full_aadder_and_sub_1_bit full_aadder_and_sub_1_bit_3: pin names not known; wires that end beside it: A2, B2, full_aadder_and_sub_1_bit_2_p6, in_5, p3, full_aadder_and_sub_1_bit_3_p6
  // full_aadder_and_sub_1_bit full_aadder_and_sub_1_bit_4: pin names not known; wires that end beside it: A3, B3, full_aadder_and_sub_1_bit_3_p6, in_5, p4, cout
endmodule
