// Digital circuit 8bit adder.dig as structural Verilog
module _8bit_adder (
  input  A1,
  input  A2,
  input  A3,
  input  A4,
  input  in_5,
  input  B0,
  input  B1,
  input  B2,
  input  B3,
  input  B4,
  input  B5,
  input  B6,
  input  B7,
  input  A5,
  input  A6,
  input  A7,
  input  A8,
  input  cin,
  output p1,
  output p2,
  output p3,
  output p4,
  output p5,
  output p6,
  output p7,
  output p8,
  output cout
);

  wire _4bit_adder_1_p12;

  // _4bit_adder _4bit_adder_1: pin names not known; wires that end beside it: A8, A7, A6, A5, in_5, p6, B7, B6, B5, B4, p5, _4bit_adder_1_p12, _4bit_adder_1_p12, p4, A4, A3, A2, p3, A1
  // _4bit_adder _4bit_adder_2: pin names not known; wires that end beside it: in_5, p2, B3, B2, B1, B0, p1, cin
endmodule
