// Digital circuit 8bit multiplier.dig as structural Verilog
module _8bit_multiplier (
  input  A0,
  input  A1,
  input  A2,
  input  A3,
  input  A4,
  input  A5,
  input  A6,
  input  A7,
  input  B0,
  input  B1,
  input  B2,
  input  B3,
  input  B4,
  input  B5,
  input  B6,
  input  B7,
  output p0,
  output p1,
  output p2,
  output p3,
  output p4,
  output p5,
  output p6,
  output p7,
  output p8,
  output p9,
  output p10,
  output p11,
  output p12,
  output p13,
  output p14,
  output p15
);

  wire _8bit_adder_1_p1, _8bit_adder_1_p2, _8bit_adder_1_p3, _8bit_adder_1_p4, _8bit_adder_1_p5,
       _8bit_adder_1_p6, _8bit_adder_1_p7, _8bit_adder_1_p8, _8bit_adder_1_p9, _8bit_adder_1_p11,
       _8bit_adder_1_p12, _8bit_adder_1_p13, _8bit_adder_1_p14, _8bit_adder_1_p15, _8bit_adder_1_p16,
       _8bit_adder_1_p17, _8bit_adder_1_p18, _8bit_adder_2_p1, _8bit_adder_2_p2, _8bit_adder_2_p3,
       _8bit_adder_2_p4, _8bit_adder_2_p5, _8bit_adder_2_p6, _8bit_adder_2_p7, _8bit_adder_2_p8,
       _8bit_adder_2_p14, _8bit_adder_2_p15, _8bit_adder_2_p16, _8bit_adder_2_p17, _8bit_adder_3_p1,
       _8bit_adder_3_p2, _8bit_adder_3_p3, _8bit_adder_3_p4, _8bit_adder_3_p5, _8bit_adder_3_p6,
       _8bit_adder_3_p7, _8bit_adder_3_p8, _8bit_adder_3_p14, _8bit_adder_3_p15, _8bit_adder_3_p16,
       _8bit_adder_3_p17;

  // _4_bit_multiplier _4_bit_multiplier_1: pin names not known; wires that end beside it: B7, B6, B5, B4, A4, A5, A6, A7
  // _8bit_adder _8bit_adder_1: pin names not known; wires that end beside it: _8bit_adder_1_p1, _8bit_adder_1_p2, _8bit_adder_1_p3, _8bit_adder_1_p4, _8bit_adder_1_p5, _8bit_adder_1_p6, _8bit_adder_1_p7, _8bit_adder_1_p8, _8bit_adder_1_p9, 1'b0, _8bit_adder_1_p11, _8bit_adder_1_p12, _8bit_adder_1_p13, _8bit_adder_1_p14, _8bit_adder_1_p15, _8bit_adder_1_p16, _8bit_adder_1_p17, _8bit_adder_1_p18
  // _4_bit_multiplier _4_bit_multiplier_2: pin names not known; wires that end beside it: B7, B6, B5, B4, A0, A1, A2, A3
  // _8bit_adder _8bit_adder_2: pin names not known; wires that end beside it: _8bit_adder_2_p1, _8bit_adder_2_p2, _8bit_adder_2_p3, _8bit_adder_2_p4, _8bit_adder_2_p5, _8bit_adder_2_p6, _8bit_adder_2_p7, _8bit_adder_2_p8, 1'b0, 1'b0, 1'b0, 1'b0, 1'b0, _8bit_adder_2_p14, _8bit_adder_2_p15, _8bit_adder_2_p16, _8bit_adder_2_p17
  // _4_bit_multiplier _4_bit_multiplier_3: pin names not known; wires that end beside it: B3, B2, B1, B0, A4, A5, A6, A7
  // _8bit_adder _8bit_adder_3: pin names not known; wires that end beside it: _8bit_adder_3_p1, _8bit_adder_3_p2, _8bit_adder_3_p3, _8bit_adder_3_p4, _8bit_adder_3_p5, _8bit_adder_3_p6, _8bit_adder_3_p7, _8bit_adder_3_p8, 1'b0, 1'b0, 1'b0, 1'b0, 1'b0, _8bit_adder_3_p14, _8bit_adder_3_p15, _8bit_adder_3_p16, _8bit_adder_3_p17
  // _4_bit_multiplier _4_bit_multiplier_4: pin names not known; wires that end beside it: B3, B2, B1, B0, A0, A1, A2, A3
endmodule
