// Digital circuit full aadder and sub 1 bit.dig as structural Verilog
module full_aadder_and_sub_1_bit (
  input  A0,
  input  B0,
  input  cin,
  input  in_4,
  output out1,
  output cout
);

  wire and_1_out, and_2_out, and_3_out, or_1_out, xor_1_out, xor_3_out;

  xor xor_1 (xor_1_out, A0, B0);
  xor xor_2 (out1, xor_1_out, cin);
  xor xor_3 (xor_3_out, A0, in_4);
  and and_1 (and_1_out, cin, xor_3_out);
  and and_2 (and_2_out, cin, B0);
  and and_3 (and_3_out, xor_3_out, B0);
  or or_1 (or_1_out, and_1_out, and_2_out);
  or or_2 (cout, or_1_out, and_3_out);
endmodule
