// Digital circuit new full adder.dig as structural Verilog
module new_full_adder (
  input  A,
  input  B,
  input  cin,
  input  in_4,
  output out,
  output cout
);

  wire and_1_out, and_2_out, and_3_out, or_1_out, xor_1_out, xor_2_out;

  xor xor_1 (xor_1_out, A, B);
  xor xor_2 (xor_2_out, A, in_4);
  xor xor_3 (out, xor_1_out, cin);
  and and_1 (and_1_out, xor_2_out, cin);
  and and_2 (and_2_out, xor_2_out, B);
  and and_3 (and_3_out, B, cin);
  or or_1 (or_1_out, and_1_out, and_2_out);
  or or_2 (cout, or_1_out, and_3_out);
endmodule
