// Digital circuit the final calculator.dig as structural Verilog
module the_final_calculator (
  input  A1,
  input  B1,
  input  plus,
  input  in_4,
  input  in_5,
  input  B2,
  input  B3,
  input  B4,
  input  B5,
  input  B6,
  input  B7,
  input  B8,
  input  B9,
  input  B10,
  input  B11,
  input  B12,
  input  B13,
  input  B14,
  input  B15,
  input  B16,
  input  A2,
  input  A3,
  input  A4,
  input  A5,
  input  A6,
  input  A7,
  input  A8,
  input  A9,
  input  A10,
  input  A11,
  input  A12,
  input  A13,
  input  A14,
  input  A15,
  input  A16
);

  wire _8bit_multiplier_1_p6, _8bit_multiplier_1_p7, _8bit_multiplier_1_p8, _16_add_1_1_p1, _16_add_1_1_p2,
       _16_add_1_1_p3, _16_add_1_1_p4, _16_add_1_1_p5, _16_add_1_1_p6, _16_add_1_1_p7, _16_add_1_1_p8,
       _16_add_1_1_p9, _16_add_1_1_p10, _16_add_1_1_p11, _16_add_1_1_p12, _16_add_1_1_p13, _16_add_1_1_p14,
       _16_add_1_1_p15, _16_add_1_1_p16, _16bit_adder_1_p16, _16bit_adder_1_p18, _16bit_adder_1_p19,
       _16bit_adder_1_p20, _16bit_adder_1_p21, _16bit_adder_1_p22, _16bit_adder_1_p23, _16bit_adder_1_p24,
       _16bit_adder_1_p25, _16bit_adder_1_p26, and_1_out, and_2_out, and_3_out, and_4_out, and_5_out,
       and_9_out, and_10_out, and_11_out, and_12_out, and_13_out, and_14_out, and_15_out, and_16_out,
       and_17_out, and_18_out, and_19_out, and_20_out, and_21_out, and_22_out, and_23_out, and_24_out,
       and_25_out, and_26_out, and_27_out, and_28_out, and_29_out, and_30_out, and_31_out, and_41_out,
       and_42_out, and_43_out, and_44_out, and_45_out, and_46_out, and_47_out, and_48_out, and_59_out,
       and_60_out, and_61_out, and_62_out, and_63_out, and_64_out, and_65_out, and_66_out, and_67_out,
       and_68_out, and_69_out, and_70_out, and_71_out, and_72_out, and_73_out, and_74_out, and_75_out,
       and_76_out, and_77_out, and_78_out, and_79_out, and_80_out, and_81_out, not_1_out, not_2_out,
       not_3_out, not_4_out, not_5_out, not_6_out, not_7_out, not_8_out, not_9_out, not_10_out, not_11_out,
       not_12_out, not_13_out, not_14_out, not_15_out, not_16_out, not_17_out, or_1_out, or_2_out, or_3_out,
       or_4_out, or_5_out, or_6_out, or_7_out, or_8_out, or_9_out, or_10_out, or_11_out, or_12_out,
       or_13_out, or_14_out, or_15_out, or_16_out, or_17_out, or_18_out, or_19_out, or_20_out, or_21_out,
       or_22_out, or_23_out, or_24_out, or_25_out, or_26_out, or_27_out, or_28_out, or_29_out, or_30_out,
       or_31_out, or_32_out, or_33_out, undriven, undriven_2, undriven_3, undriven_4, undriven_5, undriven_6,
       undriven_7, undriven_8, undriven_9, undriven_10, undriven_11, undriven_12, undriven_13, undriven_14,
       undriven_15, undriven_16, undriven_17, undriven_18, undriven_19, undriven_20, undriven_21,
       undriven_22, undriven_23, undriven_24, undriven_25, undriven_26, undriven_27, undriven_28,
       undriven_29, undriven_30, undriven_31, undriven_32, undriven_33, undriven_34, undriven_35,
       undriven_36, undriven_37, undriven_38, undriven_39, undriven_40, undriven_41, undriven_42;

  and and_1 (and_1_out, A8, in_5);
  and and_2 (and_2_out, A7, in_5);
  and and_3 (and_3_out, A6, in_5);
  and and_4 (and_4_out, A5, in_5);
  and and_5 (and_5_out, A4, in_5);
  // _8bit_multiplier _8bit_multiplier_1: pin names not known; wires that end beside it: and_1_out, and_2_out, and_3_out, and_4_out, and_5_out, _8bit_multiplier_1_p6, _8bit_multiplier_1_p7, _8bit_multiplier_1_p8
  and and_6 (_8bit_multiplier_1_p6, A3, in_5);
  and and_7 (_8bit_multiplier_1_p7, A2, in_5);
  and and_8 (_8bit_multiplier_1_p8, A1, in_5);
  and and_9 (and_9_out, B8, in_5);
  and and_10 (and_10_out, B7, in_5);
  and and_11 (and_11_out, B6, in_5);
  and and_12 (and_12_out, B5, in_5);
  and and_13 (and_13_out, B4, in_5);
  and and_14 (and_14_out, B3, in_5);
  and and_15 (and_15_out, B2, in_5);
  and and_16 (and_16_out, B1, in_5);
  or or_1 (or_1_out, in_4, plus);
  and and_17 (and_17_out, A16, or_1_out);
  and and_18 (and_18_out, or_1_out, A15);
  and and_19 (and_19_out, or_1_out, A14);
  and and_20 (and_20_out, or_1_out, A13);
  and and_21 (and_21_out, or_1_out, A12);
  and and_22 (and_22_out, or_1_out, A11);
  and and_23 (and_23_out, or_1_out, A10);
  and and_24 (and_24_out, or_1_out, A9);
  and and_25 (and_25_out, or_1_out, A8);
  and and_26 (and_26_out, A7, or_1_out);
  and and_27 (and_27_out, A6, or_1_out);
  and and_28 (and_28_out, A5, or_1_out);
  and and_29 (and_29_out, A4, or_1_out);
  // _16_add_1 _16_add_1_1: pin names not known; wires that end beside it: _16_add_1_1_p1, _16_add_1_1_p2, _16_add_1_1_p3, _16_add_1_1_p4, _16_add_1_1_p5, _16_add_1_1_p6, _16_add_1_1_p7, _16_add_1_1_p8, _16_add_1_1_p9, _16_add_1_1_p10, _16_add_1_1_p11, _16_add_1_1_p12, _16_add_1_1_p13, _16_add_1_1_p14, _16_add_1_1_p15, _16_add_1_1_p16
  and and_30 (and_30_out, A3, or_1_out);
  and and_31 (and_31_out, A2, or_1_out);
  // _16bit_adder _16bit_adder_1: pin names not known; wires that end beside it: and_17_out, and_18_out, and_19_out, and_20_out, and_21_out, and_22_out, and_23_out, and_24_out, and_25_out, and_26_out, and_27_out, and_28_out, and_29_out, and_30_out, and_31_out, _16bit_adder_1_p16, in_4, _16bit_adder_1_p18, _16bit_adder_1_p19, _16bit_adder_1_p20, _16bit_adder_1_p21, _16bit_adder_1_p22, _16bit_adder_1_p23, _16bit_adder_1_p24, _16bit_adder_1_p25, _16bit_adder_1_p26
  and and_32 (_16bit_adder_1_p16, A1, or_1_out);
  and and_33 (_16_add_1_1_p6, not_1_out, _16_add_1_1_p5);
  and and_34 (_16_add_1_1_p7, not_2_out, _16_add_1_1_p5);
  and and_35 (_16_add_1_1_p8, not_3_out, _16_add_1_1_p5);
  and and_36 (_16_add_1_1_p9, not_4_out, _16_add_1_1_p5);
  and and_37 (_16_add_1_1_p10, not_5_out, _16_add_1_1_p5);
  and and_38 (_16_add_1_1_p11, not_6_out, _16_add_1_1_p5);
  and and_39 (_16_add_1_1_p12, not_7_out, _16_add_1_1_p5);
  and and_40 (_16_add_1_1_p13, not_8_out, _16_add_1_1_p5);
  and and_41 (and_41_out, not_9_out, _16_add_1_1_p5);
  and and_42 (and_42_out, not_10_out, _16_add_1_1_p5);
  and and_43 (and_43_out, not_11_out, _16_add_1_1_p5);
  and and_44 (and_44_out, not_12_out, _16_add_1_1_p5);
  and and_45 (and_45_out, not_13_out, _16_add_1_1_p5);
  and and_46 (and_46_out, not_14_out, _16_add_1_1_p5);
  and and_47 (and_47_out, not_15_out, _16_add_1_1_p5);
  and and_48 (and_48_out, not_16_out, _16_add_1_1_p5);
  and and_49 (_16bit_adder_1_p18, B16, or_1_out);
  not not_1 (not_1_out, undriven_23);
  not not_2 (not_2_out, undriven_22);
  not not_3 (not_3_out, undriven_21);
  not not_4 (not_4_out, undriven_20);
  not not_5 (not_5_out, undriven_19);
  not not_6 (not_6_out, undriven_18);
  not not_7 (not_7_out, undriven_17);
  not not_8 (not_8_out, undriven_16);
  not not_9 (not_9_out, undriven_15);
  not not_10 (not_10_out, undriven_14);
  not not_11 (not_11_out, undriven_13);
  not not_12 (not_12_out, undriven_12);
  not not_13 (not_13_out, undriven_11);
  not not_14 (not_14_out, undriven_10);
  not not_15 (not_15_out, _16_add_1_1_p16);
  not not_16 (not_16_out, _16_add_1_1_p15);
  and and_50 (_16bit_adder_1_p19, B15, or_1_out);
  and and_51 (_16bit_adder_1_p20, B14, or_1_out);
  and and_52 (_16bit_adder_1_p21, B13, or_1_out);
  and and_53 (_16_add_1_1_p5, _16_add_1_1_p14, in_4);
  not not_17 (not_17_out, _16_add_1_1_p5);
  and and_54 (_16bit_adder_1_p22, B12, or_1_out);
  and and_55 (_16bit_adder_1_p23, B11, or_1_out);
  and and_56 (_16bit_adder_1_p24, B10, or_1_out);
  and and_57 (_16bit_adder_1_p25, B9, or_1_out);
  LED led (.in(_16_add_1_1_p5));
  LED p1 (.in(or_2_out));
  LED p2 (.in(or_4_out));
  LED p3 (.in(or_5_out));
  LED p4 (.in(or_7_out));
  LED p5 (.in(or_10_out));
  LED p6 (.in(or_12_out));
  LED p7 (.in(or_13_out));
  LED p8 (.in(or_15_out));
  LED p9 (.in(or_18_out));
  LED p10 (.in(or_20_out));
  LED p11 (.in(or_21_out));
  LED p12 (.in(or_23_out));
  LED p13 (.in(or_26_out));
  LED p14 (.in(or_28_out));
  LED p15 (.in(or_29_out));
  LED p16 (.in(or_31_out));
  and and_58 (_16bit_adder_1_p26, B8, or_1_out);
  and and_59 (and_59_out, B7, or_1_out);
  and and_60 (and_60_out, B6, or_1_out);
  and and_61 (and_61_out, B5, or_1_out);
  and and_62 (and_62_out, not_17_out, undriven_23);
  and and_63 (and_63_out, undriven_22, not_17_out);
  and and_64 (and_64_out, undriven_21, not_17_out);
  and and_65 (and_65_out, undriven_20, not_17_out);
  and and_66 (and_66_out, undriven_19, not_17_out);
  and and_67 (and_67_out, undriven_18, not_17_out);
  and and_68 (and_68_out, undriven_17, not_17_out);
  and and_69 (and_69_out, undriven_16, not_17_out);
  and and_70 (and_70_out, undriven_15, not_17_out);
  and and_71 (and_71_out, undriven_14, not_17_out);
  and and_72 (and_72_out, undriven_13, not_17_out);
  and and_73 (and_73_out, undriven_12, not_17_out);
  and and_74 (and_74_out, undriven_11, not_17_out);
  and and_75 (and_75_out, undriven_10, not_17_out);
  and and_76 (and_76_out, _16_add_1_1_p16, not_17_out);
  and and_77 (and_77_out, _16_add_1_1_p15, not_17_out);
  and and_78 (and_78_out, B4, or_1_out);
  and and_79 (and_79_out, B3, or_1_out);
  and and_80 (and_80_out, B2, or_1_out);
  and and_81 (and_81_out, B1, or_1_out);
  or or_2 (or_2_out, undriven_24, or_3_out);
  or or_3 (or_3_out, and_62_out, _16_add_1_1_p1);
  or or_4 (or_4_out, undriven_25, or_6_out);
  or or_5 (or_5_out, undriven_26, or_8_out);
  or or_6 (or_6_out, and_63_out, _16_add_1_1_p2);
  or or_7 (or_7_out, undriven_27, or_9_out);
  or or_8 (or_8_out, and_64_out, _16_add_1_1_p3);
  or or_9 (or_9_out, and_65_out, _16_add_1_1_p4);
  or or_10 (or_10_out, undriven_28, or_11_out);
  or or_11 (or_11_out, and_66_out, undriven_8);
  or or_12 (or_12_out, undriven_29, or_14_out);
  or or_13 (or_13_out, undriven_31, or_16_out);
  or or_14 (or_14_out, and_67_out, undriven_30);
  or or_15 (or_15_out, undriven_33, or_17_out);
  or or_16 (or_16_out, and_68_out, undriven_32);
  or or_17 (or_17_out, and_69_out, undriven_7);
  or or_18 (or_18_out, undriven_34, or_19_out);
  or or_19 (or_19_out, and_70_out, undriven_6);
  or or_20 (or_20_out, undriven_35, or_22_out);
  or or_21 (or_21_out, undriven_36, or_24_out);
  or or_22 (or_22_out, and_71_out, undriven_5);
  or or_23 (or_23_out, undriven_37, or_25_out);
  or or_24 (or_24_out, and_72_out, undriven_4);
  or or_25 (or_25_out, and_73_out, undriven_38);
  or or_26 (or_26_out, undriven_39, or_27_out);
  or or_27 (or_27_out, and_74_out, undriven_9);
  or or_28 (or_28_out, undriven_42, or_30_out);
  or or_29 (or_29_out, undriven_40, or_32_out);
  or or_30 (or_30_out, and_75_out, undriven_3);
  or or_31 (or_31_out, undriven_41, or_33_out);
  or or_32 (or_32_out, and_76_out, undriven_2);
  or or_33 (or_33_out, and_77_out, undriven);
endmodule
